// Logisim project s-mips.circ as structural Verilog
module S_MIPS_Board (
  input  DESHABILITAR_DISPATCHER,
  output halt
);

  wire button_1_out, CLK, CS, d_ff_1_q, LCLR, LoadRAM, LoadRAMOn, LW, R_R_W, R_W, ram_dispatcher_1_finished,
       RCS, Reset_out, RST, TTY_EN;
  wire [2:0] KDB;
  wire [3:0] LMask, Mask, ram_1_read_time, ram_1_write_time, RMask;
  wire [6:0] KDB_DATA, TTY_DATA;
  wire [15:0] Addr, LAddr, RAddr;
  wire [31:0] I0, I1, I2, I3, LData, ram_1_data_out_0, ram_1_data_out_1, ram_1_data_out_2, ram_1_data_out_3,
       RI0, RI1, RI2, RI3;

  TTY #(.rows(25), .cols(80)) tty_1 (.data(TTY_DATA), .clk(CLK), .we(TTY_EN), .clr(RST));
  not not_1 (LoadRAMOn, ram_dispatcher_1_finished);
  RAM_Dispatcher ram_dispatcher_1 (
    .WriteTime(ram_1_write_time), .Clock(CLK), .Data(LData), .Address(LAddr), .Mask(LMask),
    .Finished(ram_dispatcher_1_finished), .Write(LW), .CLR(LCLR));
  Keyboard #(.buflen(64)) keyboard_1 (.clk(CLK), .re(KDB[0]), .avail(KDB[2]), .data(KDB_DATA));  // open: clr
  RAM ram_1 (
    .Address(RAddr), .Data_Out_0(ram_1_data_out_0), .Data_Out_1(ram_1_data_out_1),
    .Data_Out_2(ram_1_data_out_2), .Data_Out_3(ram_1_data_out_3), .Data_In_0(RI0), .Data_In_1(RI1),
    .Data_In_2(RI2), .Data_In_3(RI3), .Mask(RMask), .nRead_Write(R_R_W), .Chip_Select(RCS),
    .Read_Time(ram_1_read_time), .Reset(button_1_out), .Write_Time(ram_1_write_time));
  Button button_1 (.out(button_1_out));
  D_Flip_Flop d_ff_1 (.clk(CLK), .D(1'b1), .Q(d_ff_1_q), .reset(Reset_out));  // open: Qn, preset, en
  Button Reset (.out(Reset_out));
  S_MIPS s_mips_1 (
    .Kbd_Enable(KDB[0]), .Address(Addr), .Kbd_Clear(KDB[1]), .Kbd_Available(KDB[2]), .RAM_In_0(I0),
    .Kbd_ASCII_Data(KDB_DATA), .RAM_In_1(I1), .TTY_Enable(TTY_EN), .RAM_In_2(I2), .RAM_In_3(I3),
    .TTY_ASCII_Data(TTY_DATA), .Reset(RST), .RAM_Out_0(ram_1_data_out_0), .Clock(CLK),
    .RAM_Out_1(ram_1_data_out_1), .Stop(halt), .RAM_Out_2(ram_1_data_out_2), .RAM_Out_3(ram_1_data_out_3),
    .Mask(Mask), .Read_Time(ram_1_read_time), .Write_Time(ram_1_write_time), .nRead_Write(R_W),
    .Chip_Select(CS));
  D_Flip_Flop d_ff_2 (.clk(CLK), .D(d_ff_1_q), .Qn(LCLR), .reset(Reset_out));  // open: Q, preset, en
  or or_1 (RST, LCLR, LoadRAM);
  Clock clock_1 (.out(CLK));
  Multiplexer #(.width(32), .enable("false")) multiplexer_1 (.in0(I0), .in1(LData), .out(RI0), .sel(LoadRAM));
  Multiplexer #(.width(32), .enable("false")) multiplexer_2 (.in0(I1), .in1(LData), .out(RI1), .sel(LoadRAM));
  Multiplexer #(.width(32), .enable("false")) multiplexer_3 (.in0(I2), .in1(LData), .out(RI2), .sel(LoadRAM));
  Multiplexer #(.width(32), .enable("false")) multiplexer_4 (.in0(I3), .in1(LData), .out(RI3), .sel(LoadRAM));
  and and_1 (LoadRAM, ~DESHABILITAR_DISPATCHER, LoadRAMOn);  // AND_Gate
  Multiplexer #(.width(16), .enable("false")) multiplexer_5 (.in0(Addr), .in1(LAddr), .out(RAddr), .sel(LoadRAM));
  Multiplexer #(.width(4), .enable("false")) multiplexer_6 (.in0(Mask), .in1(LMask), .out(RMask), .sel(LoadRAM));
  Multiplexer #(.enable("false")) multiplexer_7 (.in0(CS), .in1(LW), .out(RCS), .sel(LoadRAM));
  Multiplexer #(.enable("false")) multiplexer_8 (.in0(R_W), .in1(LW), .out(R_R_W), .sel(LoadRAM));

  // Notes on the sheet:
  //   NO MODIFICAR
  //   Keyboard
endmodule

module RAM (
  input  [15:0] Address,
  input  [31:0] Data_In_0,
  input  [31:0] Data_In_1,
  input  [31:0] Data_In_2,
  input  [31:0] Data_In_3,
  input  [3:0] Mask,
  input  nRead_Write,
  input  Chip_Select,
  input  Reset,
  output [31:0] Data_Out_0,
  output [31:0] Data_Out_1,
  output [31:0] Data_Out_2,
  output [31:0] Data_Out_3,
  output [3:0] Read_Time,
  output [3:0] Write_Time
);

  wire and_2_out, and_3_out, and_4_out, and_5_out, and_6_out, and_7_out, and_8_out, and_9_out, Changed, CLK,
       comparator_2_eq, comparator_3_eq, comparator_4_eq, comparator_5_eq, comparator_6_eq, Count,
       demultiplexer_3_out0, Idle, Idle_q, Load, Load0, Load1, nand_1_out, or_1_out, or_2_out, or_3_out,
       or_4_out, or_5_out, or_6_out, or_7_out, or_8_out, or_9_out, or_10_out, Proc_q, Update_Mem, Zero_Time;
  wire [3:0] counter_1_q, multiplexer_1_out, subtractor_1_out;
  wire [31:0] register_1_q, register_2_q, register_3_q, register_4_q, register_5_q;

  // Probe on 4'b0011
  // Probe on 4'b0010
  Multiplexer #(.width(4), .enable("false")) multiplexer_1 (
    .in0(4'b0011), .in1(4'b0010), .out(multiplexer_1_out), .sel(nRead_Write));
  or or_1 (or_1_out, Idle, Update_Mem);
  or or_2 (or_2_out, ~Chip_Select, Reset);  // OR_Gate
  Subtractor #(.width(4)) subtractor_1 (.a(multiplexer_1_out), .b(4'b0010), .out(subtractor_1_out));  // open: bin, bout
  D_Flip_Flop u_Idle (.clk(CLK), .D(or_1_out), .Q(Idle_q), .preset(or_2_out));  // open: Qn, en, reset
  Demultiplexer #(.enable("false")) demultiplexer_1 (.out0(Idle), .out1(Load0), .in(Idle_q), .sel(Changed));
  // Probe on counter_1_q
  Counter #(.width(4), .max('hf)) counter_1 (
    .load(Load), .D(subtractor_1_out), .count(Count), .Q(counter_1_q), .clk(CLK), .clr(or_3_out));  // open: carry
  or or_3 (or_3_out, ~Chip_Select, Reset);  // OR_Gate
  Comparator #(.width(4), .mode("unsigned")) comparator_1 (
    .a(4'b0000), .b(counter_1_q), .eq(Zero_Time));  // open: gt, lt
  or or_4 (or_4_out, Count, Load0, Load1);
  Register_part #(.width(32)) register_1 (.D(Data_In_0), .en(Chip_Select), .Q(register_1_q), .clk(CLK), .clr(or_5_out));
  or or_5 (or_5_out, ~Chip_Select, Reset);  // OR_Gate
  Register_part #(.width(32)) register_2 (.D(Data_In_1), .en(Chip_Select), .Q(register_2_q), .clk(CLK), .clr(or_6_out));
  or or_6 (or_6_out, ~Chip_Select, Reset);  // OR_Gate
  Register_part #(.width(32)) register_3 (.D(Data_In_2), .en(Chip_Select), .Q(register_3_q), .clk(CLK), .clr(or_7_out));
  or or_7 (or_7_out, ~Chip_Select, Reset);  // OR_Gate
  Register_part #(.width(32)) register_4 (.D(Data_In_3), .en(Chip_Select), .Q(register_4_q), .clk(CLK), .clr(or_8_out));
  or or_8 (or_8_out, ~Chip_Select, Reset);  // OR_Gate
  Register_part #(.width(32)) register_5 (
    .D({{11{1'b1}}, nRead_Write, Mask, Address}), .en(Chip_Select), .Q(register_5_q), .clk(CLK),
    .clr(or_9_out));
  or or_9 (or_9_out, ~Chip_Select, Reset);  // OR_Gate
  D_Flip_Flop Proc (.clk(CLK), .D(or_4_out), .Q(Proc_q), .reset(or_10_out));  // open: Qn, preset, en
  or or_10 (or_10_out, ~Chip_Select, Reset);  // OR_Gate
  Demultiplexer #(.enable("false")) demultiplexer_2 (
    .out0(Count), .out1(Update_Mem), .in(demultiplexer_3_out0), .sel(Zero_Time));
  Demultiplexer #(.enable("false")) demultiplexer_3 (
    .out0(demultiplexer_3_out0), .out1(Load1), .in(Proc_q), .sel(Changed));
  Clock clock_1 (.out(CLK));
  Comparator #(.width(32)) comparator_2 (.a(register_1_q), .b(Data_In_0), .eq(comparator_2_eq));  // open: gt, lt
  Comparator #(.width(32)) comparator_3 (.a(register_2_q), .b(Data_In_1), .eq(comparator_3_eq));  // open: gt, lt
  Comparator #(.width(32)) comparator_4 (.a(register_3_q), .b(Data_In_2), .eq(comparator_4_eq));  // open: gt, lt
  Comparator #(.width(32)) comparator_5 (.a(register_4_q), .b(Data_In_3), .eq(comparator_5_eq));  // open: gt, lt
  Comparator #(.width(32)) comparator_6 (
    .a(register_5_q), .b({{11{1'b1}}, nRead_Write, Mask, Address}), .eq(comparator_6_eq));  // open: gt, lt
  nand nand_1 (nand_1_out, comparator_6_eq, comparator_2_eq, comparator_3_eq, comparator_4_eq, comparator_5_eq);
  and and_1 (Changed, nand_1_out, Chip_Select);
  or or_11 (Load, Count, Load1, Load0);
  and and_2 (and_2_out, Mask[0], Update_Mem, nRead_Write);
  and and_3 (and_3_out, Mask[1], Update_Mem, nRead_Write);
  and and_4 (and_4_out, Mask[2], Update_Mem, nRead_Write);
  and and_5 (and_5_out, Mask[3], Update_Mem, nRead_Write);
  RAM_part #(.addrWidth(16), .dataWidth(32), .bus("separate")) ram_1 (
    .addr(Address), .din(Data_In_0), .data(Data_Out_0), .str(and_2_out), .sel(Chip_Select), .clk(CLK),
    .ld(and_6_out), .clr(Reset));
  and and_6 (and_6_out, ~nRead_Write, Idle);  // AND_Gate
  RAM_part #(.addrWidth(16), .dataWidth(32), .bus("separate")) ram_2 (
    .addr(Address), .din(Data_In_1), .data(Data_Out_1), .str(and_3_out), .sel(Chip_Select), .clk(CLK),
    .ld(and_7_out), .clr(Reset));
  and and_7 (and_7_out, ~nRead_Write, Idle);  // AND_Gate
  RAM_part #(.addrWidth(16), .dataWidth(32), .bus("separate")) ram_3 (
    .addr(Address), .din(Data_In_2), .data(Data_Out_2), .str(and_4_out), .sel(Chip_Select), .clk(CLK),
    .ld(and_8_out), .clr(Reset));
  and and_8 (and_8_out, ~nRead_Write, Idle);  // AND_Gate
  RAM_part #(.addrWidth(16), .dataWidth(32), .bus("separate")) ram_4 (
    .addr(Address), .din(Data_In_3), .data(Data_Out_3), .str(and_5_out), .sel(Chip_Select), .clk(CLK),
    .ld(and_9_out), .clr(Reset));
  and and_9 (and_9_out, ~nRead_Write, Idle);  // AND_Gate

  assign Read_Time = 4'b0011;
  assign Write_Time = 4'b0010;

  // Other names for the same wires on the sheet: M0 = Mask[0]; M1 = Mask[1]; M2 = Mask[2]; M3 = Mask[3];
  //   RW = nRead_Write; CLR = Reset; CS = Chip_Select; Load2 = Count

  // Notes on the sheet:
  //   NO MODIFICAR
  //   excepto quizás los valores RT y WT
  //   BANK0
  //   BANK1
  //   BANK2
  //   BANK3
endmodule

module S_MIPS (
  input  Kbd_Available,
  input  [6:0] Kbd_ASCII_Data,
  input  [31:0] RAM_Out_0,
  input  [31:0] RAM_Out_1,
  input  Reset,
  input  [31:0] RAM_Out_2,
  input  Clock,
  input  [31:0] RAM_Out_3,
  input  [3:0] Read_Time,
  input  [3:0] Write_Time,
  output Kbd_Enable,
  output [15:0] Address,
  output Kbd_Clear,
  output TTY_Enable,
  output [6:0] TTY_ASCII_Data,
  output Stop,
  output [31:0] RAM_In_0,
  output [31:0] RAM_In_1,
  output [31:0] RAM_In_2,
  output [31:0] RAM_In_3,
  output [3:0] Mask,
  output nRead_Write,
  output Chip_Select
);


  // Other names for the same wires on the sheet: CLK = Clock; CLR = Reset; CS = Chip_Select;
  //   KBD_AVAIL = Kbd_Available; KBD_CLR = Kbd_Clear; KBD_DATA[6:0] = Kbd_ASCII_Data; RAM_A[15:0] = Address;
  //   RAM_INPUT_0[31:0] = RAM_In_0; RAM_INPUT_1[31:0] = RAM_In_1; RAM_INPUT_2[31:0] = RAM_In_2;
  //   RAM_INPUT_3[31:0] = RAM_In_3; RAM_MASK[3:0] = Mask; RAM_OUTPUT_0[31:0] = RAM_Out_0;
  //   RAM_OUTPUT_1[31:0] = RAM_Out_1; RAM_OUTPUT_2[31:0] = RAM_Out_2; RAM_OUTPUT_3[31:0] = RAM_Out_3;
  //   RW = nRead_Write; TTY_DATA[6:0] = TTY_ASCII_Data

  // Notes on the sheet:
  //   RAM ADDRESS
  //   DATA FROM RAM
  //   DATA TO RAM
  //   DATA WRITE MASK
  //   RAM TIMING
  //   RAM CONTROL
  //   KEYBOARD
  //   TTY
  //   SEQUENCING
endmodule

module RAM_Dispatcher (
  input  [3:0] WriteTime,
  input  Clock,
  input  CLR,
  output [31:0] Data,
  output [15:0] Address,
  output [3:0] Mask,
  output Finished,
  output Write
);

  wire demultiplexer_2_out1, demultiplexer_3_out1, End, IDLE_q, IncAddr, Load, or_1_out, or_2_out, While_q,
       WriteEnd;
  wire [3:0] counter_1_q;
  wire [31:0] CurrentAddress_q;

  Counter #(.width(32), .max('hffffffff)) CurrentAddress (
    .count(IncAddr), .Q({CurrentAddress_q[31:18], Address, CurrentAddress_q[1:0]}), .clk(Clock), .clr(CLR));  // open: load, D, carry
  or or_1 (or_1_out, IncAddr, demultiplexer_3_out1, Finished);
  D_Flip_Flop IDLE (.clk(Clock), .D(or_1_out), .Q(IDLE_q), .preset(CLR));  // open: Qn, en, reset
  Demultiplexer #(.enable("false")) demultiplexer_1 (.out0(Load), .out1(Finished), .in(IDLE_q), .sel(End));
  D_Flip_Flop While (.clk(Clock), .D(or_2_out), .Q(While_q), .reset(CLR));  // open: Qn, preset, en
  or or_2 (or_2_out, Write, Load);
  RAM_part #(.addrWidth(18), .dataWidth(32)) ram_1 (
    .addr({Address, CurrentAddress_q[1:0]}), .data(Data), .clk(Clock));  // open: sel, ld, clr
  Demultiplexer #(.enable("false")) demultiplexer_2 (
    .out0(Write), .out1(demultiplexer_2_out1), .in(While_q), .sel(WriteEnd));
  Decoder #(.select(2)) decoder_1 (
    .out0(Mask[0]), .out1(Mask[1]), .out2(Mask[2]), .out3(Mask[3]), .sel(CurrentAddress_q[1:0]));  // open: en
  Demultiplexer #(.enable("false")) demultiplexer_3 (
    .out0(IncAddr), .out1(demultiplexer_3_out1), .in(demultiplexer_2_out1), .sel(End));
  Counter #(.width(4), .max('hf)) counter_1 (
    .load(Load), .D(WriteTime), .count(Write), .Q(counter_1_q), .clk(Clock));  // open: carry, clr
  Comparator #(.width(32)) comparator_1 (.a(Data), .b({32{1'b1}}), .eq(End));  // open: gt, lt
  Comparator #(.width(4)) comparator_2 (.a(4'b0000), .b(counter_1_q), .eq(WriteEnd));  // open: gt, lt

  // Other names for the same wires on the sheet: CLK = Clock; Count = Write; WT[3:0] = WriteTime
endmodule

module Adder (
  input  [31:0] Bit_1,
  input  [31:0] Bit_2,
  input  Bit_1_Sign,
  input  Bit_2_Sign,
  output Carry,
  output [31:0] Sum
);

  wire adder_1_cout, and_1_out, and_2_out, and_3_out, Clock_out, comparator_1_eq, comparator_1_gt, not_1_out,
       not_2_out, or_1_out, or_2_out, or_3_out;
  wire [31:0] adder_1_out, multiplexer_1_out, register_1_output, register_2_output, register_3_output,
       register_4_output, register_5_output, subtractor_1_out, subtractor_2_out;

  Clock Clock (.out(Clock_out));
  and and_1 (and_1_out, Bit_1_Sign, Bit_2_Sign);
  Register register_1 (.Clock(Clock_out), .Bit(Bit_1), .Output(register_1_output));
  Register register_2 (.Clock(Clock_out), .Bit(Bit_2), .Output(register_2_output));
  or or_1 (or_1_out, Bit_1_Sign, Bit_2_Sign);
  not not_1 (not_1_out, or_1_out);
  or or_2 (or_2_out, and_1_out, not_1_out);
  not not_2 (not_2_out, or_2_out);
  Comparator #(.width(32)) comparator_1 (.a(Bit_1), .b(Bit_2), .gt(comparator_1_gt), .eq(comparator_1_eq));  // open: lt
  Adder_part #(.width(32)) adder_1 (
    .a(register_1_output), .b(register_2_output), .out(adder_1_out), .cout(adder_1_cout));  // open: cin
  Subtractor #(.width(32)) subtractor_1 (
    .a(register_1_output), .b(register_2_output), .out(subtractor_1_out));  // open: bin, bout
  Subtractor #(.width(32)) subtractor_2 (
    .a(register_2_output), .b(register_1_output), .out(subtractor_2_out));  // open: bin, bout
  and and_2 (and_2_out, not_2_out, comparator_1_eq);
  and and_3 (and_3_out, not_2_out, comparator_1_gt);
  or or_3 (or_3_out, and_2_out, and_3_out);
  Register register_3 (.Clock(Clock_out), .Bit(adder_1_out), .Output(register_3_output));
  Register register_4 (.Clock(Clock_out), .Bit(subtractor_1_out), .Output(register_4_output));
  Register register_5 (.Clock(Clock_out), .Bit(subtractor_2_out), .Output(register_5_output));
  Multiplexer #(.width(32)) multiplexer_1 (
    .in0(register_4_output), .in1(register_5_output), .out(multiplexer_1_out), .sel(or_3_out));  // open: en
  Multiplexer #(.width(32)) multiplexer_2 (
    .in0(multiplexer_1_out), .in1(register_3_output), .out(Sum), .sel(or_2_out));  // open: en
  D_Flip_Flop #(.trigger("falling")) d_ff_1 (
    .clk(Clock_out), .D(adder_1_cout), .Q(Carry));  // open: Qn, preset, en, reset
endmodule

module Multiplier (
  input  [31:0] Carry_Input,
  input  [31:0] Bit_1,
  input  [31:0] Bit_2,
  input  Bit_1_Sign,
  input  Bit_2_Sign,
  output [31:0] Output,
  output [31:0] Carry_Output,
  output Sign
);

  wire and_1_out, not_1_out, or_1_out;

  and and_1 (and_1_out, Bit_1_Sign, Bit_2_Sign);
  or or_1 (or_1_out, Bit_1_Sign, Bit_2_Sign);
  not not_1 (not_1_out, or_1_out);
  Multiplier_part #(.width(32)) multiplier_1 (
    .a(Bit_1), .b(Bit_2), .out(Output), .cin(Carry_Input), .cout(Carry_Output));
  or or_2 (Sign, and_1_out, not_1_out);
endmodule

module Unsigned_Multiplier (
  input  [31:0] Carry_Input,
  input  [31:0] Bit_1,
  input  [31:0] Bit_2,
  output [31:0] Output,
  output [31:0] Carry_Output
);

  Multiplier_part #(.width(32)) multiplier_1 (
    .a(Bit_1), .b(Bit_2), .out(Output), .cin(Carry_Input), .cout(Carry_Output));
endmodule

module AlgorithmDivider (
  input  [31:0] Dividend,
  input  [31:0] Divisor,
  output [31:0] Solution,
  output [31:0] Rest
);

  Divider #(.width(32)) divider_1 (.a(Dividend), .b(Divisor), .out(Solution), .rem(Rest));  // open: upper
endmodule

module AlgorithmDivider_With_Sign (
  input  [31:0] Dividend,
  input  [31:0] Divisor,
  input  Bit_1_Sig,
  input  Bit_2_Sign,
  output [31:0] Solution,
  output [31:0] Rest,
  output Sign
);

  wire and_1_out, not_1_out, or_1_out;

  and and_1 (and_1_out, Bit_1_Sig, Bit_2_Sign);
  or or_1 (or_1_out, Bit_2_Sign, Bit_1_Sig);
  not not_1 (not_1_out, or_1_out);
  Divider #(.width(32)) divider_1 (.a(Dividend), .b(Divisor), .out(Solution), .rem(Rest));  // open: upper
  or or_2 (Sign, and_1_out, not_1_out);
endmodule

module Inmediate_Adittion (
  input  [31:0] Bit_1,
  input  [31:0] in_2,
  output [31:0] Output,
  output Output_2
);

  Adder_part #(.width(32)) adder_1 (.a(Bit_1), .b(in_2), .out(Output), .cout(Output_2));  // open: cin
endmodule

module Register (
  input  Clock,
  input  [31:0] Bit,
  output [31:0] Output
);

  D_Flip_Flop #(.trigger("falling")) d_ff_1 (.clk(Clock), .D(Bit[16]), .Q(Output[16]));  // open: Qn, preset, en, reset
  D_Flip_Flop #(.trigger("falling")) d_ff_2 (.clk(Clock), .D(Bit[17]), .Q(Output[17]));  // open: Qn, preset, en, reset
  D_Flip_Flop #(.trigger("falling")) d_ff_3 (.clk(Clock), .D(Bit[18]), .Q(Output[18]));  // open: Qn, preset, en, reset
  D_Flip_Flop #(.trigger("falling")) d_ff_4 (.clk(Clock), .D(Bit[19]), .Q(Output[19]));  // open: Qn, preset, en, reset
  D_Flip_Flop #(.trigger("falling")) d_ff_5 (.clk(Clock), .D(Bit[20]), .Q(Output[20]));  // open: Qn, preset, en, reset
  D_Flip_Flop #(.trigger("falling")) d_ff_6 (.clk(Clock), .D(Bit[21]), .Q(Output[21]));  // open: Qn, preset, en, reset
  D_Flip_Flop #(.trigger("falling")) d_ff_7 (.clk(Clock), .D(Bit[22]), .Q(Output[22]));  // open: Qn, preset, en, reset
  D_Flip_Flop #(.trigger("falling")) d_ff_8 (.clk(Clock), .D(Bit[23]), .Q(Output[23]));  // open: Qn, preset, en, reset
  D_Flip_Flop #(.trigger("falling")) d_ff_9 (.clk(Clock), .D(Bit[24]), .Q(Output[24]));  // open: Qn, preset, en, reset
  D_Flip_Flop #(.trigger("falling")) d_ff_10 (.clk(Clock), .D(Bit[25]), .Q(Output[25]));  // open: Qn, preset, en, reset
  D_Flip_Flop #(.trigger("falling")) d_ff_11 (.clk(Clock), .D(Bit[26]), .Q(Output[26]));  // open: Qn, preset, en, reset
  D_Flip_Flop #(.trigger("falling")) d_ff_12 (.clk(Clock), .D(Bit[27]), .Q(Output[27]));  // open: Qn, preset, en, reset
  D_Flip_Flop #(.trigger("falling")) d_ff_13 (.clk(Clock), .D(Bit[28]), .Q(Output[28]));  // open: Qn, preset, en, reset
  D_Flip_Flop #(.trigger("falling")) d_ff_14 (.clk(Clock), .D(Bit[29]), .Q(Output[29]));  // open: Qn, preset, en, reset
  D_Flip_Flop #(.trigger("falling")) d_ff_15 (.clk(Clock), .D(Bit[30]), .Q(Output[30]));  // open: Qn, preset, en, reset
  D_Flip_Flop #(.trigger("falling")) d_ff_16 (.clk(Clock), .D(Bit[31]), .Q(Output[31]));  // open: Qn, preset, en, reset
  D_Flip_Flop #(.trigger("falling")) d_ff_17 (.clk(Clock), .D(Bit[0]), .Q(Output[0]));  // open: Qn, preset, en, reset
  D_Flip_Flop #(.trigger("falling")) d_ff_18 (.clk(Clock), .D(Bit[1]), .Q(Output[1]));  // open: Qn, preset, en, reset
  D_Flip_Flop #(.trigger("falling")) d_ff_19 (.clk(Clock), .D(Bit[2]), .Q(Output[2]));  // open: Qn, preset, en, reset
  D_Flip_Flop #(.trigger("falling")) d_ff_20 (.clk(Clock), .D(Bit[3]), .Q(Output[3]));  // open: Qn, preset, en, reset
  D_Flip_Flop #(.trigger("falling")) d_ff_21 (.clk(Clock), .D(Bit[4]), .Q(Output[4]));  // open: Qn, preset, en, reset
  D_Flip_Flop #(.trigger("falling")) d_ff_22 (.clk(Clock), .D(Bit[5]), .Q(Output[5]));  // open: Qn, preset, en, reset
  D_Flip_Flop #(.trigger("falling")) d_ff_23 (.clk(Clock), .D(Bit[6]), .Q(Output[6]));  // open: Qn, preset, en, reset
  D_Flip_Flop #(.trigger("falling")) d_ff_24 (.clk(Clock), .D(Bit[7]), .Q(Output[7]));  // open: Qn, preset, en, reset
  D_Flip_Flop #(.trigger("falling")) d_ff_25 (.clk(Clock), .D(Bit[8]), .Q(Output[8]));  // open: Qn, preset, en, reset
  D_Flip_Flop #(.trigger("falling")) d_ff_26 (.clk(Clock), .D(Bit[9]), .Q(Output[9]));  // open: Qn, preset, en, reset
  D_Flip_Flop #(.trigger("falling")) d_ff_27 (.clk(Clock), .D(Bit[10]), .Q(Output[10]));  // open: Qn, preset, en, reset
  D_Flip_Flop #(.trigger("falling")) d_ff_28 (.clk(Clock), .D(Bit[11]), .Q(Output[11]));  // open: Qn, preset, en, reset
  D_Flip_Flop #(.trigger("falling")) d_ff_29 (.clk(Clock), .D(Bit[12]), .Q(Output[12]));  // open: Qn, preset, en, reset
  D_Flip_Flop #(.trigger("falling")) d_ff_30 (.clk(Clock), .D(Bit[13]), .Q(Output[13]));  // open: Qn, preset, en, reset
  D_Flip_Flop #(.trigger("falling")) d_ff_31 (.clk(Clock), .D(Bit[14]), .Q(Output[14]));  // open: Qn, preset, en, reset
  D_Flip_Flop #(.trigger("falling")) d_ff_32 (.clk(Clock), .D(Bit[15]), .Q(Output[15]));  // open: Qn, preset, en, reset
endmodule
